// Logisim project Frostlake_R1.6D.circ as structural Verilog: 1 circuit, main circuit main
module main (
  input  in_1,
  input  in_2,
  input  in_3,
  input  in_4
);

  wire A_RAQ, A_RBQ, ADC, ADCR, ADD, ADDR, ALU_EN, ALU_Latch, ALUOP, and_3_out, and_4_out, and_5_out,
       and_6_out, and_7_out, and_8_out, and_9_out, and_10_out, and_11_out, and_12_out, and_13_out,
       and_14_out, and_15_out, and_16_out, and_17_out, and_18_out, and_19_out, and_20_out, and_21_out,
       and_22_out, and_23_out, and_24_out, and_25_out, and_26_out, and_27_out, and_28_out, and_29_out,
       and_30_out, and_31_out, and_32_out, and_33_out, and_34_out, and_35_out, and_36_out, and_37_out,
       and_38_out, and_39_out, and_40_out, and_41_out, and_42_out, and_43_out, and_44_out, and_45_out,
       and_46_out, and_47_out, and_48_out, and_49_out, and_50_out, and_51_out, and_52_out, and_53_out,
       and_54_out, and_55_out, and_56_out, and_57_out, and_58_out, and_59_out, and_60_out, and_61_out,
       and_62_out, and_63_out, and_64_out, and_65_out, and_66_out, and_67_out, and_68_out, and_69_out,
       and_70_out, and_71_out, and_72_out, and_73_out, and_74_out, and_75_out, and_76_out, and_77_out,
       and_78_out, and_79_out, and_80_out, and_81_out, and_82_out, and_83_out, and_84_out, and_85_out,
       and_86_out, and_87_out, and_88_out, and_89_out, and_90_out, and_91_out, AOP, ASC, B_RAQ, B_RBQ, BCLK,
       C_RAQ, C_RBQ, CALL, CARRY_EN, CBR, CF, CFLAG, CLK, CMP, CMPR, controlled_buffer_16_out,
       controlled_buffer_74_out, controlled_buffer_76_out, controlled_buffer_77_out,
       controlled_buffer_79_out, controlled_buffer_80_out, controlled_buffer_114_out,
       controlled_buffer_116_out, controlled_buffer_118_out, controlled_buffer_120_out,
       controlled_buffer_121_out, controlled_buffer_191_out, controlled_buffer_195_out,
       controlled_buffer_208_out, controlled_buffer_210_out, D_RAQ, D_RBQ, Decode, DO_JMP, E_RAQ, E_RBQ,
       EN_A, EN_MAR, EN_PC, EN_RAM, EN_RAQ, EN_RBQ, EN_STCK, Execute, F_RAQ, F_RBQ, Fetch, FL_EN, FLOCK,
       G_RAQ, G_RBQ, H_RAQ, H_RBQ, IN2, IOP, JE, JGE, JLE, JMP, JNE, LDA, LDI, LOAD_A, LOAD_B, LOAD_FREG,
       LOAD_MAR, LOAD_RAM, LOAD_RAQ, LOAD_RBQ, MOP, MOV, NF, NICHT, NICHTR, NOP, not_1_out, not_2_out,
       not_4_out, not_5_out, not_6_out, not_7_out, not_8_out, not_10_out, not_11_out, not_12_out, not_13_out,
       not_14_out, not_15_out, not_16_out, not_17_out, not_18_out, not_19_out, not_20_out, ODER, ODERR,
       or_1_out, or_2_out, or_5_out, or_7_out, or_8_out, or_9_out, or_10_out, or_11_out, or_13_out,
       or_14_out, or_15_out, or_16_out, or_17_out, or_18_out, or_19_out, or_20_out, or_21_out, or_22_out,
       or_23_out, or_24_out, POP, pull_resistor_2_node, pull_resistor_21_node, PUSH, register_4_q,
       register_5_q, RET, ROP, SBB, SBBR, STA, STCK_DEC, STCK_INC, SUB, SUBR, SV_PC, UND, UNDR, VF, VFLAG,
       WRT_ADDR, WRT_DAT, ZF, ZFLAG;
  wire [0:0] controlled_buffer_148_out, controlled_buffer_150_out;
  wire [1:0] adder_2_out, Phase, SO;
  wire [1:1] controlled_buffer_173_out, controlled_buffer_174_out;
  wire [3:0] ALC, bit_extender_4_out, bit_extender_5_out, bit_extender_6_out, bit_extender_7_out,
       bit_extender_8_out, bit_extender_9_out, bit_extender_10_out, bit_extender_11_out, bit_extender_12_out,
       bit_extender_13_out, bit_extender_14_out, bit_extender_15_out;
  wire [5:0] MAR;
  wire [7:0] A_ND, adder_5_out, adder_7_out, ADR_BUS, AR, bit_extender_1_out, bit_extender_2_out,
       controlled_buffer_7_out, controlled_buffer_14_out, controlled_buffer_19_out, controlled_buffer_20_out,
       controlled_buffer_24_out, controlled_buffer_26_out, controlled_buffer_36_out,
       controlled_buffer_38_out, controlled_buffer_46_out, controlled_buffer_48_out,
       controlled_buffer_56_out, controlled_buffer_58_out, FMAR, multiplexer_1_out, N_OT, O_R, OP1, PC,
       RAM_ADDR, RAQ, RAR, RBQ, RBQA, REG_BUS, register_3_q, register_9_q, register_10_q, register_11_q,
       register_12_q, register_13_q, register_14_q, register_15_q, register_16_q, register_17_q, SUBF,
       subtractor_1_out, ZK;
  wire [7:6] OP0;
  wire [23:0] bit_extender_3_out, controlled_buffer_5_out, controlled_buffer_6_out, MEM_BUS, VRAM_dout;
  wire [23:8] controlled_buffer_13_out;
  wire [23:16] register_6_q;

  or or_1 (or_1_out, ROP, IOP);
  not not_1 (not_1_out, MOV);
  and and_1 (ALUOP, or_1_out, not_1_out);
  not not_2 (not_2_out, in_3);
  Adder adder_1 (.a(RAQ), .b(ZK), .out(RAR), .cout(CFLAG));  // open: cin
  or or_2 (or_2_out, LOAD_FREG, and_3_out);
  // Probe on RAR
  // Probe on CFLAG
  // Probe on N_OT
  assign N_OT = ~RAQ;  // NOT_Gate not_3, 8 bits wide
  // Probe on A_ND
  assign A_ND = RAQ & RBQA;  // AND_Gate and_2, 8 bits wide
  // Probe on O_R
  assign O_R = RAQ | RBQA;  // OR_Gate or_3, 8 bits wide
  not not_4 (not_4_out, FL_EN);
  and and_3 (and_3_out, not_4_out, ALUOP);
  Register #(.width(4)) register_1 (
    .D({CFLAG, ZFLAG, AR[7], VFLAG}), .en(or_2_out), .clk(BCLK), .Q({CF, ZF, NF, VF}), .clr(in_1));
  Demultiplexer #(.select(2)) demultiplexer_1 (
    .out0(Fetch), .out1(Decode), .out2(Execute), .out3(IN2), .in(not_2_out), .sel(Phase));
  nor nor_1 (ZFLAG, AR[0], AR[1], AR[2], AR[3], AR[4], AR[5], AR[6], AR[7]);
  Adder #(.width(2)) adder_2 (.a(Phase), .b(2'b00), .out(adder_2_out), .cin(1'b1));  // open: cout
  Clock #(.highDuration(2), .lowDuration(2)) clock_1 (.out(CLK));
  assign bit_extender_1_out = {{7{ASC}}, ASC};  // Bit_Extender bit_extender_1
  Pull_Resistor pull_resistor_1 (.node(ASC));
  Register #(.width(2)) register_2 (.D(adder_2_out), .clk(CLK), .Q(Phase), .clr(in_1));  // open: en
  Register register_3 (.D(multiplexer_1_out), .en(ALU_Latch), .clk(CLK), .Q(register_3_q), .clr(in_1));
  Multiplexer #(.select(4), .width(8)) multiplexer_1 (
    .in0(N_OT), .in1(A_ND), .in2(O_R), .in4({RAQ[7], 1'b0, RAQ[6:1]}), .in5({RAQ[7], RAQ[5:0], 1'b0}),
    .in15(AR), .out(multiplexer_1_out), .sel(ALC));  // open: in3, in6, in7, in8, in9, in10, in11, in12, in13, in14
  Register #(.width(1)) register_4 (.D(pull_resistor_2_node), .en(ALUOP), .clk(CLK), .Q(register_4_q), .clr(in_1));
  Pull_Resistor pull_resistor_2 (.node(pull_resistor_2_node));
  assign pull_resistor_2_node = CFLAG ? CFLAG : 1'bz;  // Controlled_Buffer controlled_buffer_1
  // Probe on bit_extender_1_out
  or or_4 (VFLAG, and_4_out, and_5_out);
  and and_4 (and_4_out, RAQ[7], ZK[7], not_5_out);
  not not_5 (not_5_out, AR[7]);
  assign ZK = RBQA ^ bit_extender_1_out;  // XOR_Gate xor_1, 8 bits wide
  and and_5 (and_5_out, not_7_out, not_6_out, AR[7]);
  not not_6 (not_6_out, ZK[7]);
  not not_7 (not_7_out, RAQ[7]);
  assign REG_BUS = ALU_EN ? register_3_q : 8'bz;  // Controlled_Buffer controlled_buffer_2
  Pull_Resistor pull_resistor_3 (.node(CBR));
  assign CBR = CARRY_EN ? register_4_q : 1'bz;  // Controlled_Buffer controlled_buffer_3
  // Probe on ZK
  // Probe on {RAQ[7], 1'b0, RAQ[6:1]}
  // Probe on {RAQ[7], RAQ[5:0], 1'b0}
  Register #(.width(1)) register_5 (.D(not_8_out), .en(FLOCK), .clk(Decode), .Q(register_5_q), .clr(in_1));
  Pull_Resistor pull_resistor_4 (.node(FLOCK));
  not not_8 (not_8_out, register_5_q);
  Adder #(.width(1)) adder_3 (.a(ASC), .b(CBR), .out(SO[0]), .cout(SO[1]));  // open: cin
  assign bit_extender_2_out = {{6{SO[1]}}, SO};  // Bit_Extender bit_extender_2
  Pull_Resistor pull_resistor_5 (.node(FL_EN));
  assign FL_EN = register_5_q ? register_5_q : 1'bz;  // Controlled_Buffer controlled_buffer_4
  Adder adder_4 (.a(RAR), .b(bit_extender_2_out), .out(AR));  // open: cin, cout
  or or_5 (or_5_out, EN_RAM, Fetch);
  Pull_Resistor pull_resistor_6 (.node(or_5_out));
  assign controlled_buffer_5_out = Fetch ? MEM_BUS : 24'bz;  // Controlled_Buffer controlled_buffer_5
  // Probe on RAM_ADDR
  Pull_Resistor pull_resistor_7 (.node(LOAD_RAM));
  Clock clock_2 (.out(BCLK));
  assign bit_extender_3_out = {{16{1'b0}}, REG_BUS};  // Bit_Extender bit_extender_3
  assign controlled_buffer_6_out = LOAD_RAM ? bit_extender_3_out : 24'bz;  // Controlled_Buffer controlled_buffer_6
  assign controlled_buffer_7_out = LOAD_MAR ? ADR_BUS : 8'bz;  // Controlled_Buffer controlled_buffer_7
  Pull_Resistor pull_resistor_8 (.node(LOAD_MAR));
  not not_9 (WRT_DAT, WRT_ADDR);
  // Probe on ALC
  Pull_Resistor pull_resistor_9 (.node(EN_MAR));
  Pull_Resistor pull_resistor_10 (.node(EN_STCK));
  Pull_Resistor pull_resistor_11 (.node(EN_PC));
  Pull_Resistor pull_resistor_12 (.node(SV_PC));
  Pull_Resistor pull_resistor_13 (.node(LOAD_B));
  Register #(.width(24)) register_6 (
    .D(controlled_buffer_5_out), .en(Fetch), .clk(BCLK), .Q({register_6_q, OP1, OP0, MAR}), .clr(in_1));
  RAM #(.dataWidth(24)) VRAM (
    .addr(RAM_ADDR), .we(LOAD_RAM), .oe(or_5_out), .clk(BCLK), .din(controlled_buffer_6_out), .dout(VRAM_dout));
  // Probe on controlled_buffer_7_out
  Pull_Resistor pull_resistor_14 (.node(WRT_ADDR));
  Pull_Resistor pull_resistor_15 (.node(LOAD_A));
  Register register_7 (.D(controlled_buffer_7_out), .en(LOAD_MAR), .clk(CLK), .Q(FMAR), .clr(in_1));
  Pull_Resistor pull_resistor_16 (.node(STCK_INC));
  assign RAM_ADDR = EN_MAR ? FMAR : 8'bz;  // Controlled_Buffer controlled_buffer_8
  Pull_Resistor pull_resistor_17 (.node(EN_MAR));
  assign EN_RAM = Fetch ? Fetch : 1'bz;  // Controlled_Buffer controlled_buffer_9
  Pull_Resistor pull_resistor_18 (.node(EN_A));
  // Probe on VRAM_dout
  Pull_Resistor pull_resistor_19 (.node(STCK_DEC));
  assign ADR_BUS = MOP ? OP1 : 8'bz;  // Controlled_Buffer controlled_buffer_10
  assign ADR_BUS = RET ? REG_BUS : 8'bz;  // Controlled_Buffer controlled_buffer_11
  assign MEM_BUS = Fetch ? VRAM_dout : 24'bz;  // Controlled_Buffer controlled_buffer_12
  nor nor_2 (EN_PC, EN_MAR, EN_STCK);
  assign {controlled_buffer_13_out, REG_BUS} = EN_RAM ? VRAM_dout : 24'bz;  // Controlled_Buffer controlled_buffer_13
  Adder adder_5 (.a(PC), .b(8'h1), .out(adder_5_out));  // open: cin, cout
  Pull_Resistor pull_resistor_20 (.node(DO_JMP));
  not not_10 (not_10_out, DO_JMP);
  and and_6 (and_6_out, DO_JMP, CLK);
  Demultiplexer #(.select(8)) demultiplexer_2 (
    .out0(NOP), .out1(ADD), .out2(ADDR), .out3(ADC), .out4(ADCR), .out5(SUB), .out6(SUBR), .out7(SBB),
    .out8(SBBR), .out16(UND), .out17(UNDR), .out18(ODER), .out19(ODERR), .out20(NICHT), .out21(NICHTR),
    .out22(CMP), .out23(CMPR), .out48(LDI), .out49(LDA), .out50(MOV), .out51(STA), .out52(PUSH), .out53(POP),
    .out80(JMP), .out81(JE), .out82(JNE), .out83(JGE), .out84(JLE), .out85(CALL), .out86(RET), .out87(FLOCK),
    .in(1'b1), .sel(register_6_q));  // open: out9, out10, out11, out12, out13, out14, out15, out24, out25, out26, out27, out28, out29, out30, out31, out32, out33, out34, out35, out36, out37, out38, out39, out40, out41, out42, out43, out44, out45, out46, out47, out54, out55, out56, out57, out58, out59, out60, out61, out62, out63, out64, out65, out66, out67, out68, out69, out70, out71, out72, out73, out74, out75, out76, out77, out78, out79, out88, out89, out90, out91, out92, out93, out94, out95, out96, out97, out98, out99, out100, out101, out102, out103, out104, out105, out106, out107, out108, out109, out110, out111, out112, out113, out114, out115, out116, out117, out118, out119, out120, out121, out122, out123, out124, out125, out126, out127, out128, out129, out130, out131, out132, out133, out134, out135, out136, out137, out138, out139, out140, out141, out142, out143, out144, out145, out146, out147, out148, out149, out150, out151, out152, out153, out154, out155, out156, out157, out158, out159, out160, out161, out162, out163, out164, out165, out166, out167, out168, out169, out170, out171, out172, out173, out174, out175, out176, out177, out178, out179, out180, out181, out182, out183, out184, out185, out186, out187, out188, out189, out190, out191, out192, out193, out194, out195, out196, out197, out198, out199, out200, out201, out202, out203, out204, out205, out206, out207, out208, out209, out210, out211, out212, out213, out214, out215, out216, out217, out218, out219, out220, out221, out222, out223, out224, out225, out226, out227, out228, out229, out230, out231, out232, out233, out234, out235, out236, out237, out238, out239, out240, out241, out242, out243, out244, out245, out246, out247, out248, out249, out250, out251, out252, out253, out254, out255
  assign controlled_buffer_14_out = not_10_out ? adder_5_out : 8'bz;  // Controlled_Buffer controlled_buffer_14
  Register register_8 (.D(controlled_buffer_14_out), .clk(controlled_buffer_16_out), .Q(PC), .clr(in_1));  // open: en
  assign controlled_buffer_14_out = DO_JMP ? ADR_BUS : 8'bz;  // Controlled_Buffer controlled_buffer_15
  assign controlled_buffer_16_out = pull_resistor_21_node ? pull_resistor_21_node : 1'bz;  // Controlled_Buffer controlled_buffer_16
  Pull_Resistor pull_resistor_21 (.node(pull_resistor_21_node));
  or or_6 (pull_resistor_21_node, and_6_out, Decode);
  Pull_Resistor pull_resistor_22 (.node(controlled_buffer_16_out));
  assign REG_BUS = SV_PC ? PC : 8'bz;  // Controlled_Buffer controlled_buffer_17
  assign RAM_ADDR = EN_PC ? PC : 8'bz;  // Controlled_Buffer controlled_buffer_18
  Subtractor subtractor_1 (.a(register_9_q), .b(8'h1), .out(subtractor_1_out));  // open: bin, bout
  assign controlled_buffer_19_out = STCK_DEC ? subtractor_1_out : 8'bz;  // Controlled_Buffer controlled_buffer_19
  or or_7 (or_7_out, in_1, STCK_DEC, STCK_INC);
  assign controlled_buffer_20_out = WRT_ADDR ? PC : 8'bz;  // Controlled_Buffer controlled_buffer_20
  Adder adder_6 (.a(controlled_buffer_20_out), .b(8'h1), .out(SUBF));  // open: cin, cout
  assign controlled_buffer_19_out = STCK_INC ? adder_7_out : 8'bz;  // Controlled_Buffer controlled_buffer_21
  assign controlled_buffer_19_out = in_1 ? {8{1'b1}} : 8'bz;  // Controlled_Buffer controlled_buffer_22
  Adder adder_7 (.a(register_9_q), .b(8'h1), .out(adder_7_out));  // open: cin, cout
  Register register_9 (.D(controlled_buffer_19_out), .en(or_7_out), .clk(CLK), .Q(register_9_q));  // open: clr
  assign RAM_ADDR = EN_STCK ? register_9_q : 8'bz;  // Controlled_Buffer controlled_buffer_23
  Pull_Resistor pull_resistor_23 (.node(EN_STCK));
  Pull_Resistor pull_resistor_24 (.node(ADD));
  Pull_Resistor pull_resistor_25 (.node(EN_RAM));
  Pull_Resistor pull_resistor_26 (.node(EN_RAQ));
  Pull_Resistor pull_resistor_27 (.node(EN_RBQ));
  Pull_Resistor pull_resistor_28 (.node(ALU_EN));
  Pull_Resistor pull_resistor_29 (.node(LOAD_FREG));
  Pull_Resistor pull_resistor_30 (.node(LOAD_RBQ));
  Pull_Resistor pull_resistor_31 (.node(LOAD_RAQ));
  Pull_Resistor pull_resistor_32 (.node(ROP));
  Pull_Resistor pull_resistor_33 (.node(IOP));
  Pull_Resistor pull_resistor_34 (.node(MOP));
  Pull_Resistor pull_resistor_35 (.node(AOP));
  and and_7 (and_7_out, A_RAQ, EN_RAQ);
  not not_11 (not_11_out, IOP);
  and and_8 (and_8_out, A_RAQ, LOAD_RAQ);
  or or_8 (or_8_out, and_8_out, and_13_out);
  assign controlled_buffer_24_out = not_11_out ? REG_BUS : 8'bz;  // Controlled_Buffer controlled_buffer_24
  assign controlled_buffer_24_out = IOP ? OP1 : 8'bz;  // Controlled_Buffer controlled_buffer_25
  and and_9 (and_9_out, B_RAQ, EN_RAQ);
  assign controlled_buffer_26_out = not_12_out ? REG_BUS : 8'bz;  // Controlled_Buffer controlled_buffer_26
  assign controlled_buffer_26_out = IOP ? OP1 : 8'bz;  // Controlled_Buffer controlled_buffer_27
  not not_12 (not_12_out, IOP);
  or or_9 (or_9_out, and_7_out, and_11_out);
  and and_10 (and_10_out, B_RAQ, LOAD_RAQ);
  or or_10 (or_10_out, and_9_out, and_12_out);
  or or_11 (or_11_out, and_10_out, and_14_out);
  Register register_10 (.D(controlled_buffer_24_out), .en(or_8_out), .clk(CLK), .Q(register_10_q), .clr(in_1));
  Register register_11 (.D(controlled_buffer_26_out), .en(or_11_out), .clk(CLK), .Q(register_11_q), .clr(in_1));
  and and_11 (and_11_out, A_RBQ, EN_RBQ);
  assign REG_BUS = or_9_out ? register_10_q : 8'bz;  // Controlled_Buffer controlled_buffer_28
  assign RAQ = A_RAQ ? register_10_q : 8'bz;  // Controlled_Buffer controlled_buffer_29
  assign RBQ = A_RBQ ? register_10_q : 8'bz;  // Controlled_Buffer controlled_buffer_30
  and and_12 (and_12_out, B_RBQ, EN_RBQ);
  assign REG_BUS = or_10_out ? register_11_q : 8'bz;  // Controlled_Buffer controlled_buffer_31
  assign RAQ = B_RAQ ? register_11_q : 8'bz;  // Controlled_Buffer controlled_buffer_32
  assign RBQ = B_RBQ ? register_11_q : 8'bz;  // Controlled_Buffer controlled_buffer_33
  and and_13 (and_13_out, A_RBQ, LOAD_RBQ);
  and and_14 (and_14_out, B_RBQ, LOAD_RBQ);
  assign RBQA = ROP ? RBQ : 8'bz;  // Controlled_Buffer controlled_buffer_34
  Demultiplexer #(.select(3)) demultiplexer_3 (
    .out0(A_RAQ), .out1(B_RAQ), .out2(C_RAQ), .out3(D_RAQ), .out4(E_RAQ), .out5(F_RAQ), .out6(G_RAQ),
    .out7(H_RAQ), .in(1'b1), .sel(MAR[2:0]));
  assign RBQA = IOP ? OP1 : 8'bz;  // Controlled_Buffer controlled_buffer_35
  Demultiplexer #(.select(3)) demultiplexer_4 (
    .out0(A_RBQ), .out1(B_RBQ), .out2(C_RBQ), .out3(D_RBQ), .out4(E_RBQ), .out5(F_RBQ), .out6(G_RBQ),
    .out7(H_RBQ), .in(ROP), .sel(OP1[2:0]));
  or or_12 (ALU_Latch, ROP, IOP);
  and and_15 (and_15_out, C_RAQ, EN_RAQ);
  not not_13 (not_13_out, IOP);
  and and_16 (and_16_out, C_RAQ, LOAD_RAQ);
  or or_13 (or_13_out, and_16_out, and_21_out);
  assign controlled_buffer_36_out = not_13_out ? REG_BUS : 8'bz;  // Controlled_Buffer controlled_buffer_36
  assign controlled_buffer_36_out = IOP ? OP1 : 8'bz;  // Controlled_Buffer controlled_buffer_37
  and and_17 (and_17_out, D_RAQ, EN_RAQ);
  assign controlled_buffer_38_out = not_14_out ? REG_BUS : 8'bz;  // Controlled_Buffer controlled_buffer_38
  assign controlled_buffer_38_out = IOP ? OP1 : 8'bz;  // Controlled_Buffer controlled_buffer_39
  not not_14 (not_14_out, IOP);
  or or_14 (or_14_out, and_15_out, and_19_out);
  and and_18 (and_18_out, D_RAQ, LOAD_RAQ);
  or or_15 (or_15_out, and_17_out, and_20_out);
  or or_16 (or_16_out, and_18_out, and_22_out);
  Register register_12 (.D(controlled_buffer_36_out), .en(or_13_out), .clk(CLK), .Q(register_12_q), .clr(in_1));
  Register register_13 (.D(controlled_buffer_38_out), .en(or_16_out), .clk(CLK), .Q(register_13_q), .clr(in_1));
  and and_19 (and_19_out, C_RBQ, EN_RBQ);
  assign REG_BUS = or_14_out ? register_12_q : 8'bz;  // Controlled_Buffer controlled_buffer_40
  assign RAQ = C_RAQ ? register_12_q : 8'bz;  // Controlled_Buffer controlled_buffer_41
  assign RBQ = C_RBQ ? register_12_q : 8'bz;  // Controlled_Buffer controlled_buffer_42
  and and_20 (and_20_out, D_RBQ, EN_RBQ);
  assign REG_BUS = or_15_out ? register_13_q : 8'bz;  // Controlled_Buffer controlled_buffer_43
  assign RAQ = D_RAQ ? register_13_q : 8'bz;  // Controlled_Buffer controlled_buffer_44
  assign RBQ = D_RBQ ? register_13_q : 8'bz;  // Controlled_Buffer controlled_buffer_45
  and and_21 (and_21_out, C_RBQ, LOAD_RBQ);
  and and_22 (and_22_out, D_RBQ, LOAD_RBQ);
  and and_23 (and_23_out, E_RAQ, EN_RAQ);
  not not_15 (not_15_out, IOP);
  and and_24 (and_24_out, F_RAQ, EN_RAQ);
  not not_16 (not_16_out, IOP);
  and and_25 (and_25_out, E_RAQ, LOAD_RAQ);
  or or_17 (or_17_out, and_25_out, and_29_out);
  assign controlled_buffer_46_out = not_15_out ? REG_BUS : 8'bz;  // Controlled_Buffer controlled_buffer_46
  assign controlled_buffer_46_out = IOP ? OP1 : 8'bz;  // Controlled_Buffer controlled_buffer_47
  and and_26 (and_26_out, F_RAQ, LOAD_RAQ);
  or or_18 (or_18_out, and_26_out, and_30_out);
  assign controlled_buffer_48_out = not_16_out ? REG_BUS : 8'bz;  // Controlled_Buffer controlled_buffer_48
  assign controlled_buffer_48_out = IOP ? OP1 : 8'bz;  // Controlled_Buffer controlled_buffer_49
  or or_19 (or_19_out, and_23_out, and_27_out);
  or or_20 (or_20_out, and_24_out, and_28_out);
  Register register_14 (.D(controlled_buffer_46_out), .en(or_17_out), .clk(CLK), .Q(register_14_q), .clr(in_1));
  Register register_15 (.D(controlled_buffer_48_out), .en(or_18_out), .clk(CLK), .Q(register_15_q), .clr(in_1));
  and and_27 (and_27_out, E_RBQ, EN_RBQ);
  assign REG_BUS = or_19_out ? register_14_q : 8'bz;  // Controlled_Buffer controlled_buffer_50
  assign RAQ = E_RAQ ? register_14_q : 8'bz;  // Controlled_Buffer controlled_buffer_51
  assign RBQ = E_RBQ ? register_14_q : 8'bz;  // Controlled_Buffer controlled_buffer_52
  and and_28 (and_28_out, F_RBQ, EN_RBQ);
  assign REG_BUS = or_20_out ? register_15_q : 8'bz;  // Controlled_Buffer controlled_buffer_53
  assign RAQ = F_RAQ ? register_15_q : 8'bz;  // Controlled_Buffer controlled_buffer_54
  assign RBQ = F_RBQ ? register_15_q : 8'bz;  // Controlled_Buffer controlled_buffer_55
  and and_29 (and_29_out, E_RBQ, LOAD_RBQ);
  and and_30 (and_30_out, F_RBQ, LOAD_RBQ);
  and and_31 (and_31_out, G_RAQ, EN_RAQ);
  not not_17 (not_17_out, IOP);
  and and_32 (and_32_out, G_RAQ, LOAD_RAQ);
  or or_21 (or_21_out, and_32_out, and_37_out);
  assign controlled_buffer_56_out = not_17_out ? REG_BUS : 8'bz;  // Controlled_Buffer controlled_buffer_56
  assign controlled_buffer_56_out = IOP ? OP1 : 8'bz;  // Controlled_Buffer controlled_buffer_57
  and and_33 (and_33_out, H_RAQ, EN_RAQ);
  assign controlled_buffer_58_out = not_18_out ? REG_BUS : 8'bz;  // Controlled_Buffer controlled_buffer_58
  assign controlled_buffer_58_out = IOP ? OP1 : 8'bz;  // Controlled_Buffer controlled_buffer_59
  not not_18 (not_18_out, IOP);
  or or_22 (or_22_out, and_31_out, and_35_out);
  and and_34 (and_34_out, H_RAQ, LOAD_RAQ);
  or or_23 (or_23_out, and_33_out, and_36_out);
  or or_24 (or_24_out, and_34_out, and_38_out);
  Register register_16 (.D(controlled_buffer_56_out), .en(or_21_out), .clk(CLK), .Q(register_16_q), .clr(in_1));
  Register register_17 (.D(controlled_buffer_58_out), .en(or_24_out), .clk(CLK), .Q(register_17_q), .clr(in_1));
  and and_35 (and_35_out, G_RBQ, EN_RBQ);
  assign REG_BUS = or_22_out ? register_16_q : 8'bz;  // Controlled_Buffer controlled_buffer_60
  assign RAQ = G_RAQ ? register_16_q : 8'bz;  // Controlled_Buffer controlled_buffer_61
  assign RBQ = G_RBQ ? register_16_q : 8'bz;  // Controlled_Buffer controlled_buffer_62
  and and_36 (and_36_out, H_RBQ, EN_RBQ);
  assign REG_BUS = or_23_out ? register_17_q : 8'bz;  // Controlled_Buffer controlled_buffer_63
  assign RAQ = H_RAQ ? register_17_q : 8'bz;  // Controlled_Buffer controlled_buffer_64
  assign RBQ = H_RBQ ? register_17_q : 8'bz;  // Controlled_Buffer controlled_buffer_65
  and and_37 (and_37_out, G_RBQ, LOAD_RBQ);
  and and_38 (and_38_out, H_RBQ, LOAD_RBQ);
  assign ROP = and_39_out ? and_39_out : 1'bz;  // Controlled_Buffer controlled_buffer_66
  and and_39 (and_39_out, ADDR, Execute);
  assign CBR = and_44_out ? and_44_out : 1'bz;  // Controlled_Buffer controlled_buffer_67
  assign CBR = and_40_out ? and_40_out : 1'bz;  // Controlled_Buffer controlled_buffer_68
  assign ROP = and_40_out ? and_40_out : 1'bz;  // Controlled_Buffer controlled_buffer_69
  and and_40 (and_40_out, ADCR, Execute);
  assign ASC = and_41_out ? and_41_out : 1'bz;  // Controlled_Buffer controlled_buffer_70
  assign IOP = and_41_out ? and_41_out : 1'bz;  // Controlled_Buffer controlled_buffer_71
  and and_41 (and_41_out, CMP, Execute);
  assign EN_STCK = and_45_out ? and_45_out : 1'bz;  // Controlled_Buffer controlled_buffer_72
  assign DO_JMP = and_42_out ? and_42_out : 1'bz;  // Controlled_Buffer controlled_buffer_73
  and and_42 (and_42_out, JMP, Decode);
  assign controlled_buffer_74_out = and_43_out ? and_43_out : 1'bz;  // Controlled_Buffer controlled_buffer_74
  assign IOP = and_43_out ? and_43_out : 1'bz;  // Controlled_Buffer controlled_buffer_75
  and and_43 (and_43_out, ADD, Execute);
  assign controlled_buffer_76_out = and_39_out ? and_39_out : 1'bz;  // Controlled_Buffer controlled_buffer_76
  Pull_Resistor pull_resistor_36 (.node(controlled_buffer_76_out));
  assign controlled_buffer_77_out = and_44_out ? and_44_out : 1'bz;  // Controlled_Buffer controlled_buffer_77
  assign IOP = and_44_out ? and_44_out : 1'bz;  // Controlled_Buffer controlled_buffer_78
  and and_44 (and_44_out, ADC, Execute);
  assign controlled_buffer_79_out = and_40_out ? and_40_out : 1'bz;  // Controlled_Buffer controlled_buffer_79
  Pull_Resistor pull_resistor_37 (.node(controlled_buffer_79_out));
  assign controlled_buffer_80_out = and_41_out ? and_41_out : 1'bz;  // Controlled_Buffer controlled_buffer_80
  Pull_Resistor pull_resistor_38 (.node(controlled_buffer_80_out));
  assign EN_RAQ = and_45_out ? and_45_out : 1'bz;  // Controlled_Buffer controlled_buffer_81
  and and_45 (and_45_out, PUSH, Decode);
  assign MOP = and_42_out ? and_42_out : 1'bz;  // Controlled_Buffer controlled_buffer_82
  assign bit_extender_4_out = {{3{controlled_buffer_74_out}}, controlled_buffer_74_out};  // Bit_Extender bit_extender_4
  Pull_Resistor pull_resistor_39 (.node(controlled_buffer_74_out));
  assign bit_extender_5_out = {{3{controlled_buffer_76_out}}, controlled_buffer_76_out};  // Bit_Extender bit_extender_5
  assign ALC = controlled_buffer_76_out ? bit_extender_5_out : 4'bz;  // Controlled_Buffer controlled_buffer_83
  assign bit_extender_6_out = {{3{controlled_buffer_77_out}}, controlled_buffer_77_out};  // Bit_Extender bit_extender_6
  Pull_Resistor pull_resistor_40 (.node(controlled_buffer_77_out));
  assign bit_extender_7_out = {{3{controlled_buffer_79_out}}, controlled_buffer_79_out};  // Bit_Extender bit_extender_7
  assign ALC = controlled_buffer_79_out ? bit_extender_7_out : 4'bz;  // Controlled_Buffer controlled_buffer_84
  assign bit_extender_8_out = {{3{controlled_buffer_80_out}}, controlled_buffer_80_out};  // Bit_Extender bit_extender_8
  assign ALC = controlled_buffer_80_out ? bit_extender_8_out : 4'bz;  // Controlled_Buffer controlled_buffer_85
  assign LOAD_RAM = and_45_out ? and_45_out : 1'bz;  // Controlled_Buffer controlled_buffer_86
  assign DO_JMP = and_46_out ? and_46_out : 1'bz;  // Controlled_Buffer controlled_buffer_87
  and and_46 (and_46_out, JE, Decode, ZF);
  assign ALC = controlled_buffer_74_out ? bit_extender_4_out : 4'bz;  // Controlled_Buffer controlled_buffer_88
  assign ALU_EN = and_47_out ? and_47_out : 1'bz;  // Controlled_Buffer controlled_buffer_89
  and and_47 (and_47_out, ADDR, IN2);
  assign ALC = controlled_buffer_77_out ? bit_extender_6_out : 4'bz;  // Controlled_Buffer controlled_buffer_90
  assign ALU_EN = and_48_out ? and_48_out : 1'bz;  // Controlled_Buffer controlled_buffer_91
  and and_48 (and_48_out, ADCR, IN2);
  assign ALU_EN = and_49_out ? and_49_out : 1'bz;  // Controlled_Buffer controlled_buffer_92
  and and_49 (and_49_out, CMP, IN2);
  assign MOP = and_46_out ? and_46_out : 1'bz;  // Controlled_Buffer controlled_buffer_93
  assign ALU_EN = and_50_out ? and_50_out : 1'bz;  // Controlled_Buffer controlled_buffer_94
  assign LOAD_RAQ = and_50_out ? and_50_out : 1'bz;  // Controlled_Buffer controlled_buffer_95
  and and_50 (and_50_out, ADD, IN2);
  assign LOAD_RAQ = and_47_out ? and_47_out : 1'bz;  // Controlled_Buffer controlled_buffer_96
  assign ALU_EN = and_51_out ? and_51_out : 1'bz;  // Controlled_Buffer controlled_buffer_97
  assign LOAD_RAQ = and_51_out ? and_51_out : 1'bz;  // Controlled_Buffer controlled_buffer_98
  and and_51 (and_51_out, ADC, IN2);
  assign LOAD_RAQ = and_48_out ? and_48_out : 1'bz;  // Controlled_Buffer controlled_buffer_99
  assign LOAD_FREG = and_49_out ? and_49_out : 1'bz;  // Controlled_Buffer controlled_buffer_100
  assign STCK_DEC = and_52_out ? and_52_out : 1'bz;  // Controlled_Buffer controlled_buffer_101
  and and_52 (and_52_out, PUSH, Execute);
  assign CBR = and_54_out ? and_54_out : 1'bz;  // Controlled_Buffer controlled_buffer_102
  assign DO_JMP = and_53_out ? and_53_out : 1'bz;  // Controlled_Buffer controlled_buffer_103
  assign MOP = and_53_out ? and_53_out : 1'bz;  // Controlled_Buffer controlled_buffer_104
  and and_53 (and_53_out, JNE, Decode, not_19_out);
  not not_19 (not_19_out, ZF);
  assign ASC = and_57_out ? and_57_out : 1'bz;  // Controlled_Buffer controlled_buffer_105
  assign ASC = and_58_out ? and_58_out : 1'bz;  // Controlled_Buffer controlled_buffer_106
  assign CBR = and_59_out ? and_59_out : 1'bz;  // Controlled_Buffer controlled_buffer_107
  assign ASC = and_59_out ? and_59_out : 1'bz;  // Controlled_Buffer controlled_buffer_108
  assign ASC = and_54_out ? and_54_out : 1'bz;  // Controlled_Buffer controlled_buffer_109
  assign ROP = and_54_out ? and_54_out : 1'bz;  // Controlled_Buffer controlled_buffer_110
  and and_54 (and_54_out, SBBR, Execute);
  assign ASC = and_55_out ? and_55_out : 1'bz;  // Controlled_Buffer controlled_buffer_111
  assign ROP = and_55_out ? and_55_out : 1'bz;  // Controlled_Buffer controlled_buffer_112
  and and_55 (and_55_out, CMPR, Execute);
  assign STCK_INC = and_56_out ? and_56_out : 1'bz;  // Controlled_Buffer controlled_buffer_113
  and and_56 (and_56_out, POP, Decode);
  assign controlled_buffer_114_out = and_57_out ? and_57_out : 1'bz;  // Controlled_Buffer controlled_buffer_114
  assign IOP = and_57_out ? and_57_out : 1'bz;  // Controlled_Buffer controlled_buffer_115
  and and_57 (and_57_out, SUB, Execute);
  assign controlled_buffer_116_out = and_58_out ? and_58_out : 1'bz;  // Controlled_Buffer controlled_buffer_116
  assign ROP = and_58_out ? and_58_out : 1'bz;  // Controlled_Buffer controlled_buffer_117
  and and_58 (and_58_out, SUBR, Execute);
  assign controlled_buffer_118_out = and_59_out ? and_59_out : 1'bz;  // Controlled_Buffer controlled_buffer_118
  assign IOP = and_59_out ? and_59_out : 1'bz;  // Controlled_Buffer controlled_buffer_119
  and and_59 (and_59_out, SBB, Execute);
  assign controlled_buffer_120_out = and_54_out ? and_54_out : 1'bz;  // Controlled_Buffer controlled_buffer_120
  Pull_Resistor pull_resistor_41 (.node(controlled_buffer_120_out));
  assign controlled_buffer_121_out = and_55_out ? and_55_out : 1'bz;  // Controlled_Buffer controlled_buffer_121
  Pull_Resistor pull_resistor_42 (.node(controlled_buffer_121_out));
  assign DO_JMP = and_60_out ? and_60_out : 1'bz;  // Controlled_Buffer controlled_buffer_122
  assign MOP = and_60_out ? and_60_out : 1'bz;  // Controlled_Buffer controlled_buffer_123
  and and_60 (and_60_out, JGE, Decode, VF);
  assign bit_extender_9_out = {{3{controlled_buffer_114_out}}, controlled_buffer_114_out};  // Bit_Extender bit_extender_9
  Pull_Resistor pull_resistor_43 (.node(controlled_buffer_114_out));
  assign bit_extender_10_out = {{3{controlled_buffer_116_out}}, controlled_buffer_116_out};  // Bit_Extender bit_extender_10
  assign ALC = controlled_buffer_116_out ? bit_extender_10_out : 4'bz;  // Controlled_Buffer controlled_buffer_124
  Pull_Resistor pull_resistor_44 (.node(controlled_buffer_116_out));
  assign bit_extender_11_out = {{3{controlled_buffer_118_out}}, controlled_buffer_118_out};  // Bit_Extender bit_extender_11
  assign ALC = controlled_buffer_118_out ? bit_extender_11_out : 4'bz;  // Controlled_Buffer controlled_buffer_125
  Pull_Resistor pull_resistor_45 (.node(controlled_buffer_118_out));
  assign bit_extender_12_out = {{3{controlled_buffer_120_out}}, controlled_buffer_120_out};  // Bit_Extender bit_extender_12
  assign ALC = controlled_buffer_120_out ? bit_extender_12_out : 4'bz;  // Controlled_Buffer controlled_buffer_126
  assign bit_extender_13_out = {{3{controlled_buffer_121_out}}, controlled_buffer_121_out};  // Bit_Extender bit_extender_13
  assign ALC = controlled_buffer_121_out ? bit_extender_13_out : 4'bz;  // Controlled_Buffer controlled_buffer_127
  assign EN_STCK = and_63_out ? and_63_out : 1'bz;  // Controlled_Buffer controlled_buffer_128
  assign ALC = controlled_buffer_114_out ? bit_extender_9_out : 4'bz;  // Controlled_Buffer controlled_buffer_129
  assign ALU_EN = and_61_out ? and_61_out : 1'bz;  // Controlled_Buffer controlled_buffer_130
  and and_61 (and_61_out, SBBR, IN2);
  assign ALU_EN = and_62_out ? and_62_out : 1'bz;  // Controlled_Buffer controlled_buffer_131
  and and_62 (and_62_out, CMPR, IN2);
  assign LOAD_RAQ = and_63_out ? and_63_out : 1'bz;  // Controlled_Buffer controlled_buffer_132
  and and_63 (and_63_out, POP, Execute);
  assign DO_JMP = and_64_out ? and_64_out : 1'bz;  // Controlled_Buffer controlled_buffer_133
  assign MOP = and_64_out ? and_64_out : 1'bz;  // Controlled_Buffer controlled_buffer_134
  and and_64 (and_64_out, JLE, Decode, not_20_out);
  not not_20 (not_20_out, VF);
  assign ALU_EN = and_65_out ? and_65_out : 1'bz;  // Controlled_Buffer controlled_buffer_135
  assign LOAD_RAQ = and_65_out ? and_65_out : 1'bz;  // Controlled_Buffer controlled_buffer_136
  and and_65 (and_65_out, SUB, IN2);
  assign ALU_EN = and_66_out ? and_66_out : 1'bz;  // Controlled_Buffer controlled_buffer_137
  assign LOAD_RAQ = and_66_out ? and_66_out : 1'bz;  // Controlled_Buffer controlled_buffer_138
  and and_66 (and_66_out, SUBR, IN2);
  assign ALU_EN = and_67_out ? and_67_out : 1'bz;  // Controlled_Buffer controlled_buffer_139
  assign LOAD_RAQ = and_67_out ? and_67_out : 1'bz;  // Controlled_Buffer controlled_buffer_140
  and and_67 (and_67_out, SBB, IN2);
  assign LOAD_RAQ = and_61_out ? and_61_out : 1'bz;  // Controlled_Buffer controlled_buffer_141
  assign LOAD_FREG = and_62_out ? and_62_out : 1'bz;  // Controlled_Buffer controlled_buffer_142
  assign EN_RAM = and_63_out ? and_63_out : 1'bz;  // Controlled_Buffer controlled_buffer_143
  assign ASC = and_69_out ? and_69_out : 1'bz;  // Controlled_Buffer controlled_buffer_144
  assign ASC = and_70_out ? and_70_out : 1'bz;  // Controlled_Buffer controlled_buffer_145
  assign LOAD_RAQ = and_68_out ? and_68_out : 1'bz;  // Controlled_Buffer controlled_buffer_146
  and and_68 (and_68_out, LDI, Decode);
  assign EN_STCK = and_71_out ? and_71_out : 1'bz;  // Controlled_Buffer controlled_buffer_147
  assign controlled_buffer_148_out[0] = and_69_out ? and_69_out : 1'bz;  // Controlled_Buffer controlled_buffer_148
  assign IOP = and_69_out ? and_69_out : 1'bz;  // Controlled_Buffer controlled_buffer_149
  and and_69 (and_69_out, UND, Execute);
  assign controlled_buffer_150_out[0] = and_70_out ? and_70_out : 1'bz;  // Controlled_Buffer controlled_buffer_150
  assign ROP = and_70_out ? and_70_out : 1'bz;  // Controlled_Buffer controlled_buffer_151
  and and_70 (and_70_out, UNDR, Execute);
  assign IOP = and_68_out ? and_68_out : 1'bz;  // Controlled_Buffer controlled_buffer_152
  assign SV_PC = and_71_out ? and_71_out : 1'bz;  // Controlled_Buffer controlled_buffer_153
  assign LOAD_RAM = and_71_out ? and_71_out : 1'bz;  // Controlled_Buffer controlled_buffer_154
  and and_71 (and_71_out, CALL, Decode);
  Pull_Resistor pull_resistor_46 (.node(controlled_buffer_148_out[0]));
  assign ALC = controlled_buffer_150_out[0] ? {3'b000, controlled_buffer_150_out[0]} : 4'bz;  // Controlled_Buffer controlled_buffer_155
  Pull_Resistor pull_resistor_47 (.node(controlled_buffer_150_out[0]));
  assign LOAD_MAR = and_72_out ? and_72_out : 1'bz;  // Controlled_Buffer controlled_buffer_156
  and and_72 (and_72_out, LDA, Decode);
  assign ALC = controlled_buffer_148_out[0] ? {3'b000, controlled_buffer_148_out[0]} : 4'bz;  // Controlled_Buffer controlled_buffer_157
  assign MOP = and_72_out ? and_72_out : 1'bz;  // Controlled_Buffer controlled_buffer_158
  assign ALU_EN = and_73_out ? and_73_out : 1'bz;  // Controlled_Buffer controlled_buffer_159
  assign LOAD_RAQ = and_73_out ? and_73_out : 1'bz;  // Controlled_Buffer controlled_buffer_160
  and and_73 (and_73_out, UND, IN2);
  assign ALU_EN = and_74_out ? and_74_out : 1'bz;  // Controlled_Buffer controlled_buffer_161
  assign LOAD_RAQ = and_74_out ? and_74_out : 1'bz;  // Controlled_Buffer controlled_buffer_162
  and and_74 (and_74_out, UNDR, IN2);
  assign EN_MAR = and_76_out ? and_76_out : 1'bz;  // Controlled_Buffer controlled_buffer_163
  assign STCK_DEC = and_75_out ? and_75_out : 1'bz;  // Controlled_Buffer controlled_buffer_164
  and and_75 (and_75_out, CALL, Execute);
  assign LOAD_RAQ = and_76_out ? and_76_out : 1'bz;  // Controlled_Buffer controlled_buffer_165
  and and_76 (and_76_out, LDA, Execute);
  assign DO_JMP = and_75_out ? and_75_out : 1'bz;  // Controlled_Buffer controlled_buffer_166
  assign ASC = and_77_out ? and_77_out : 1'bz;  // Controlled_Buffer controlled_buffer_167
  assign IOP = and_77_out ? and_77_out : 1'bz;  // Controlled_Buffer controlled_buffer_168
  and and_77 (and_77_out, ODER, Execute);
  assign ASC = and_78_out ? and_78_out : 1'bz;  // Controlled_Buffer controlled_buffer_169
  assign ROP = and_78_out ? and_78_out : 1'bz;  // Controlled_Buffer controlled_buffer_170
  and and_78 (and_78_out, ODERR, Execute);
  assign EN_RAM = and_76_out ? and_76_out : 1'bz;  // Controlled_Buffer controlled_buffer_171
  assign MOP = and_75_out ? and_75_out : 1'bz;  // Controlled_Buffer controlled_buffer_172
  assign controlled_buffer_173_out[1] = and_77_out ? and_77_out : 1'bz;  // Controlled_Buffer controlled_buffer_173
  Pull_Resistor pull_resistor_48 (.node(controlled_buffer_173_out[1]));
  assign controlled_buffer_174_out[1] = and_78_out ? and_78_out : 1'bz;  // Controlled_Buffer controlled_buffer_174
  Pull_Resistor pull_resistor_49 (.node(controlled_buffer_174_out[1]));
  assign ALC = controlled_buffer_173_out[1] ? {2'b00, controlled_buffer_173_out[1], 1'b0} : 4'bz;  // Controlled_Buffer controlled_buffer_175
  assign ALC = controlled_buffer_174_out[1] ? {2'b00, controlled_buffer_174_out[1], 1'b0} : 4'bz;  // Controlled_Buffer controlled_buffer_176
  assign LOAD_RAQ = and_79_out ? and_79_out : 1'bz;  // Controlled_Buffer controlled_buffer_177
  and and_79 (and_79_out, MOV, Execute);
  assign EN_STCK = and_80_out ? and_80_out : 1'bz;  // Controlled_Buffer controlled_buffer_178
  and and_80 (and_80_out, RET, Decode);
  assign ALU_EN = and_81_out ? and_81_out : 1'bz;  // Controlled_Buffer controlled_buffer_179
  and and_81 (and_81_out, ODER, IN2);
  assign ALU_EN = and_82_out ? and_82_out : 1'bz;  // Controlled_Buffer controlled_buffer_180
  and and_82 (and_82_out, ODERR, IN2);
  assign EN_RBQ = and_79_out ? and_79_out : 1'bz;  // Controlled_Buffer controlled_buffer_181
  assign EN_RAM = and_80_out ? and_80_out : 1'bz;  // Controlled_Buffer controlled_buffer_182
  assign LOAD_RAQ = and_81_out ? and_81_out : 1'bz;  // Controlled_Buffer controlled_buffer_183
  assign LOAD_RAQ = and_82_out ? and_82_out : 1'bz;  // Controlled_Buffer controlled_buffer_184
  assign ROP = and_79_out ? and_79_out : 1'bz;  // Controlled_Buffer controlled_buffer_185
  assign DO_JMP = and_80_out ? and_80_out : 1'bz;  // Controlled_Buffer controlled_buffer_186
  assign LOAD_MAR = and_83_out ? and_83_out : 1'bz;  // Controlled_Buffer controlled_buffer_187
  and and_83 (and_83_out, STA, Decode);
  assign ASC = and_84_out ? and_84_out : 1'bz;  // Controlled_Buffer controlled_buffer_188
  assign IOP = and_84_out ? and_84_out : 1'bz;  // Controlled_Buffer controlled_buffer_189
  and and_84 (and_84_out, NICHT, Execute);
  assign ASC = and_85_out ? and_85_out : 1'bz;  // Controlled_Buffer controlled_buffer_190
  assign controlled_buffer_191_out = and_85_out ? and_85_out : 1'bz;  // Controlled_Buffer controlled_buffer_191
  assign ROP = and_85_out ? and_85_out : 1'bz;  // Controlled_Buffer controlled_buffer_192
  and and_85 (and_85_out, NICHTR, Execute);
  assign MOP = and_83_out ? and_83_out : 1'bz;  // Controlled_Buffer controlled_buffer_193
  assign STCK_DEC = and_86_out ? and_86_out : 1'bz;  // Controlled_Buffer controlled_buffer_194
  and and_86 (and_86_out, RET, Execute);
  assign controlled_buffer_195_out = and_84_out ? and_84_out : 1'bz;  // Controlled_Buffer controlled_buffer_195
  Pull_Resistor pull_resistor_50 (.node(controlled_buffer_195_out));
  Pull_Resistor pull_resistor_51 (.node(controlled_buffer_191_out));
  assign ALC = controlled_buffer_195_out ? 4'b0000 : 4'bz;  // Controlled_Buffer controlled_buffer_196
  assign ALC = controlled_buffer_191_out ? 4'b0000 : 4'bz;  // Controlled_Buffer controlled_buffer_197
  assign EN_MAR = and_89_out ? and_89_out : 1'bz;  // Controlled_Buffer controlled_buffer_198
  assign ALU_EN = and_87_out ? and_87_out : 1'bz;  // Controlled_Buffer controlled_buffer_199
  and and_87 (and_87_out, NICHT, IN2);
  assign ALU_EN = and_88_out ? and_88_out : 1'bz;  // Controlled_Buffer controlled_buffer_200
  assign LOAD_RAQ = and_88_out ? and_88_out : 1'bz;  // Controlled_Buffer controlled_buffer_201
  and and_88 (and_88_out, NICHTR, IN2);
  assign EN_RAQ = and_89_out ? and_89_out : 1'bz;  // Controlled_Buffer controlled_buffer_202
  assign LOAD_RAM = and_89_out ? and_89_out : 1'bz;  // Controlled_Buffer controlled_buffer_203
  and and_89 (and_89_out, STA, Execute);
  assign LOAD_RAQ = and_87_out ? and_87_out : 1'bz;  // Controlled_Buffer controlled_buffer_204
  assign ASC = and_90_out ? and_90_out : 1'bz;  // Controlled_Buffer controlled_buffer_205
  assign IOP = and_90_out ? and_90_out : 1'bz;  // Controlled_Buffer controlled_buffer_206
  and and_90 (and_90_out, CMP, Execute);
  assign ASC = and_91_out ? and_91_out : 1'bz;  // Controlled_Buffer controlled_buffer_207
  assign controlled_buffer_208_out = and_91_out ? and_91_out : 1'bz;  // Controlled_Buffer controlled_buffer_208
  assign ROP = and_91_out ? and_91_out : 1'bz;  // Controlled_Buffer controlled_buffer_209
  and and_91 (and_91_out, CMPR, Execute);
  assign controlled_buffer_210_out = and_90_out ? and_90_out : 1'bz;  // Controlled_Buffer controlled_buffer_210
  Pull_Resistor pull_resistor_52 (.node(controlled_buffer_210_out));
  assign bit_extender_14_out = {{3{controlled_buffer_208_out}}, controlled_buffer_208_out};  // Bit_Extender bit_extender_14
  Pull_Resistor pull_resistor_53 (.node(controlled_buffer_208_out));
  assign bit_extender_15_out = {{3{controlled_buffer_210_out}}, controlled_buffer_210_out};  // Bit_Extender bit_extender_15
  assign ALC = controlled_buffer_210_out ? bit_extender_15_out : 4'bz;  // Controlled_Buffer controlled_buffer_211
  assign LOAD_FREG = controlled_buffer_210_out ? controlled_buffer_210_out : 1'bz;  // Controlled_Buffer controlled_buffer_212
  assign ALC = controlled_buffer_208_out ? bit_extender_14_out : 4'bz;  // Controlled_Buffer controlled_buffer_213
  assign LOAD_FREG = controlled_buffer_208_out ? controlled_buffer_208_out : 1'bz;  // Controlled_Buffer controlled_buffer_214

  // Other names for the same wires on the sheet: OP0[5:0] = MAR; NFLAG = AR[7]; CLR_RAM = in_2; EN_B = in_4;
  //   HLT = in_3; IN0 = Decode; IN1 = Execute; SHTL[7:1] = {RAQ[7], RAQ[5:0]}; SHTR (some bits) = RAQ[7:1];
  //   START = in_1; WriteBack = IN2
endmodule
